# Fritzing sketch Schéma électrique Etiqueteuse (saved by Fritzing 0.9.3b)
circuit board: 31.0468cm x 21.1512cm
breadboards: 2

parts:
  M1 = fc-51 [package=THT]
  M2 = fc-51 [package=THT]
  M3 = fc-51 [package=THT]
  M4 = fc-51 [package=THT]
  Composant1 = Arduino Uno (Rev3) - ICSP
  U1 = Module 4 Relais 5V [package="Module 4 Relais 5V"]
  S1 = Toggle Switch [package=THT]
  M5 = linear actuator [package=THT]
  M6 = linear actuator [package=THT]
  J1 = Power Jack [package=power_jack_pth]

nets (from the breadboard view):
  N1: M1.pin1, Composant1.D5_PWM
  GND: M1.pin2, M2.pin2, M3.pin2, M4.pin2, Composant1.GND, U1.GND
  N2: M1.pin3, M2.pin3, M3.pin3, M4.pin3, Composant1.5V
  N3: M2.pin1, Composant1.D2
  N4: M3.pin1, Composant1.D3_PWM
  N5: M4.pin1, Composant1.D4
  N6: Composant1.D12/MISO, U1.IN3, U1.IN4
  N7: Composant1.D13/SCK, U1.IN1, U1.IN2
  N8: Composant1.D7, S1.COM
  N9: U1.K1-NF, U1.K3-NF, S1.L2, J1.PWR
  N10: U1.K2-NF, U1.K4-NF, S1.L1, J1.GND
  N11: U1.K1-Com, U1.K2-NO, M5.pin1
  N12: U1.K2-Com, U1.K1-NO, M5.pin2
  N13: U1.K3-Com, U1.K4-NO, M6.pin1
  N14: U1.K4-Com, U1.K3-NO, M6.pin2

notes:
  Vérin Stoppeur
  [Vérin Etiqueteuse]
  Capteur de bouteille pour vérin stoppeur
  Capteur de bouteille pour vérin étiqueteuse
  Capteur de bouteille

custom parts:
  Module 4 Relais 5V: Module 4 Relais 5V 4x SPD-06VDC-SD-C
  linear actuator: Generic linear actuator.

// code stored in the sketch: Untitled.ino
// Programmation Etiqueteuse
#include <Arduino.h>
#include <NewPing.h>
#include <Bounce2.h>



#define CMD_VER_STOP 13 
#define CMD_VER_LABEL 12 
#define DISTANCE_DETECT 5 
#define DISTANCE_MAX 20 
#define TIME_DELAY 2000
#define LABEL_TIMER 2000
#define DEBUG_TIMER 1000
#define SECURITY_TIMER 3000 
#define CAPT_VER_STOP1 2
#define CAPT_VER_STOP2 3
#define CAPT_LABEL 4
#define CAPT_END 5
#define DEBUG_BUTTON 7


Bounce captBottleStop1 = Bounce();
Bounce captBottleStop2 = Bounce();
Bounce captBottleLabel = Bounce();
Bounce captBottleEnd = Bounce();
Bounce debugButton = Bounce();



/**
 * @Graph1 => Graph du vérin d'entrée (0-3)
 * @Graph2 => Graph du vérin étiquette
 * @Graph3 => Graph étiquetteuse
 * @Graph4 => Graph Encombrement
 * @Graph5 => Graph Débuggage
 */
int Graph1Step = 0, Graph2Step = 0, Graph3step = 0, Graph4Step = 0, Graph5Step = 0;


/**
 * @brief setup est exécuté lors du premier tour de cycle et ne sera pas jamais appellé.
 * @arg : none
 * @return : none
 */
void setup(){
  
  pinMode(CMD_VER_STOP, OUTPUT);
  pinMode(CMD_VER_LABEL, OUTPUT); 
  digitalWrite(CMD_VER_STOP, LOW); 
  digitalWrite(CMD_VER_LABEL, HIGH);
  captBottleStop1.attach(CAPT_VER_STOP1,  INPUT_PULLUP );
  captBottleStop1.interval(50); 
  captBottleStop2.attach(CAPT_VER_STOP2,  INPUT_PULLUP );
  captBottleStop2.interval(50); 
  captBottleEnd.attach(CAPT_END, INPUT_PULLUP);
  captBottleEnd.interval(50);
  debugButton.attach(DEBUG_BUTTON, INPUT_PULLUP);
  debugButton.interval(50);
  captBottleLabel.attach(CAPT_LABEL, INPUT_PULLUP);
  captBottleLabel.interval(50);
}


void loop(){ 
  Graph1();
  Graph2();
  Graph3();
  Graph4();
  Graph5();
  
}


/**
 * @brief Graph 1 : Graph séquentiel de fonctionnement de la partie alimentation en bouteilles de l'étiquetteuse
 * @arg none
 * @return none
 * 
 */
void Graph1(){
  /* Definir les variables / constantes locales */
  
  bool bottleFinded;
  captBottleStop1.update();
  bool bottlePassed;
  captBottleStop2.update();
  
    if (Graph1Step == 0){
    /* Action réalisée sur l'étape */


    /* Gestion de la transition */
    bottleFinded = !captBottleStop1.read();
    //Serial.println(captBottleStop2.read());
    if (bottleFinded && Graph4Step == 0){
      Graph1Step = 1;
    }
   } 
  else if (Graph1Step == 1){
    /* Action réalisée sur l'étape */
    digitalWrite(CMD_VER_STOP, HIGH);
    /* Gestion de la transition */
    bottleFinded = !captBottleStop1.read();
    bottlePassed = !captBottleStop2.read();
    if (bottlePassed) {
      Graph1Step = 2;
    }
  }
  else if (Graph1Step == 2){
    /* Action réalisée sur l'étape */
    digitalWrite(CMD_VER_STOP, LOW);
    /* Gestion de la transition */
    if(Graph2Step == 5){
      Graph1Step = 3;
    }


  }
  else if (Graph1Step == 3){
    /* Action réalisée sur l'étape */
    /* Gestion de la transition */


    if(Graph2Step == 0){
      Graph1Step = 0; 
    }    
  } 
  else {
    Graph1Step = 0;
  }
}


/**
 * @brief Graph 2 : Graph séquentiel de fontionnement de la partie vérin pousseur de l'étiquetteuse
 * @arg none
 * @return none
 * 
 */
void Graph2(){
  /* Declare locales */
  captBottleLabel.update();
  bool bottleFinded;
  static unsigned long bottleDetected;


  if (Graph2Step == 0){
    bottleFinded = !captBottleLabel.read();
    if (bottleFinded){
      /* Bottle detected on the labeler --> go to step 1*/
      Graph2Step = 1;
    }
  } 
  else if (Graph2Step == 1){
    /* Push bottle */
    digitalWrite(CMD_VER_LABEL, LOW);
    /* Goto step 2 */
    Graph2Step = 2;
  }
  else if (Graph2Step == 2){
    /* Start labelling timer */
    if (bottleDetected == 0){
      bottleDetected = millis();
    }
    /* Goto step 3 */
    Graph2Step = 3;
  }
  else if (Graph2Step == 3){
    /* check if timer is over */
    if(millis() - bottleDetected >= LABEL_TIMER){
      /* Timer is over */
      /* Go to step 4 */
       Graph2Step = 4;
    }
  }
  else if (Graph2Step == 4){
    /* Retract pusher */
    digitalWrite(CMD_VER_LABEL, HIGH);
    /* reset Timer */
    bottleDetected = 0;
    bottleFinded = !captBottleLabel.read();
      if (!bottleFinded){
        Graph2Step = 5;
      }
  }
  else if (Graph2Step == 5){
    if (Graph1Step == 3){
      Graph2Step = 0;
    }
  } else {
    Graph2Step = 0;
  }
}


/**
 * @brief Graph 3 : Graph séquentiel de fonctionnement de l'étiquetteuse
 * @arg none
 * @return none
 * 
 */
void Graph3(){
  /* Declare locales */
  /*  Action réalisée sur l'étape */
  /* Gestion de la transition */
}


/**
 * @brief Graph 4 : Graph séquentiel de fonctionnement de la table d'accumulation
 * @arg none
 * @return none
 * 
 */
void Graph4(){
  /* Definir les variables / constantes locales */
  bool bottleFinded;
  captBottleEnd.update();
  static unsigned long bottleDetected;
  
  if (Graph4Step == 0){
    /* Action réalisée sur l'étape */
    /* Gestion de la transition */
    
    bottleFinded = !captBottleEnd.read();
    if (bottleFinded){
      Graph4Step = 1;
    }
   } 
  else if (Graph4Step == 1){
    /* Action réalisée sur l'étape */
    if (bottleDetected == 0){
      bottleDetected = millis();
    }
    /* Gestion des transitions */
    /* Transition vers étape 10 */
    bottleFinded = !captBottleEnd.read();
    if (!bottleFinded) {
      Graph4Step = 10;
    }
    /* Transition vers étape 20 */ 
    else if (millis() - bottleDetected >= SECURITY_TIMER){
      /* Timer is over */
      /* Go to step 20 */
      Graph4Step = 20;
    }
  }
  else if (Graph4Step == 10){
    /* Action réalisée sur l'étape */
    bottleDetected=0;
    /* Gestion de la transition */
    Graph4Step=0;
  }


  else if ( Graph4Step == 20){
     /* Action réalisée sur l'étape */
    bottleDetected=0; 
     /* Gestion de la transition */
    bottleFinded = !captBottleEnd.read();
    if(!bottleFinded){
      Graph4Step = 0;
    }
  } 
  else {
    Graph4Step = 0;
  }


}


/**
 * @brief Graph de Debbuggaga : Graph séquentiel de Débuggage
 * @arg none
 * @return none
 * 
 */
void Graph5(){
  /*  Declare locales */
  static unsigned long debbuggage;
  unsigned long currentTime;
  bool bugButton;
  debugButton.update();
  
  /* Graph */
  if (Graph5Step == 0) {
    /* Actions */
    bugButton = debugButton.read();
  if(bugButton){
    Serial.begin(9600);
      }
    /* Transitions */
    Graph5Step = 1;
  } 
  else  if (Graph5Step == 1) {
    /* Actions */
    debbuggage = millis();
    /* Transitions */
    Graph5Step = 2;
  } 
  else  if (Graph5Step == 2) {
    /* Actions */
    currentTime = millis();
    if (currentTime - debbuggage >= DEBUG_TIMER) {
      Serial.println( "********************");
      Serial.print("Graph 1 : ");
      Serial.println(Graph1Step);
      Serial.print("Graph 2 : ");
      Serial.println(Graph2Step);
      // Serial.println(Graph3Step);
      Serial.print("Graph 4 : ");
      Serial.println(Graph4Step);
      Serial.end();
    }
    /* Transitions */
    if (currentTime - debbuggage >= DEBUG_TIMER) {
      Graph5Step = 0;
    }
  } else {
    Graph5Step = 0;
  } 
}
